// Digital circuit PC.dig as structural Verilog
module PC (
  input  [31:0] \input ,
  input  reset,
  input  wen,
  input  clock,
  output [31:0] Output
);

  wire [31:0] multiplexer_1_out;

  Multiplexer #(.Bits(32)) multiplexer_1 (.sel(reset), .in_0(\input ), .in_1({32{1'b0}}), .out(multiplexer_1_out));
  Register #(.Bits(32), .isProgramCounter("true")) PC (.D(multiplexer_1_out), .C(~clock), .en(wen), .Q(Output));

  // Notes on the sheet:
  //   input: La salida actual de la ALU, este valor se usa como dirección en caso de un salto o se suma a la dirección actual
  //   Output: El contador de programa actual
  //   reset: Provoca un salto absoluto. El valor de la entrada de la ALU se utiliza como la nueva dirección
  //   wen: Se activa si hay un salto relativo. El valor de la entrada de la ALU se le suma a la dirección actual
endmodule
